// Logisim project crc.circ as structural Verilog
module _4divider (
  input  [3:0] bcs,
  input  [3:0] cs,
  output [2:0] out_3,
  output Shang
);

  wire [3:0] xor_1_out;
  wire [3:3] multiplexer_1_out;

  assign xor_1_out = bcs ^ cs;  // XOR_Gate xor_1, 4 bits wide
  Multiplexer #(.width(4)) multiplexer_1 (
    .in0(bcs), .in1(xor_1_out), .out({multiplexer_1_out[3], out_3}), .sel(bcs[3]));  // open: en

  assign Shang = bcs[3];
endmodule

module CRC (
  input  [7:0] A,
  input  [3:0] B,
  output [10:0] C
);

  wire [2:0] n4divider_1_out_3, n4divider_2_out_3, n4divider_3_out_3, n4divider_4_out_3, n4divider_5_out_3,
       n4divider_6_out_3, n4divider_7_out_3;

  _4divider u_4divider_1 (.bcs(A[7:4]), .cs(B), .out_3(n4divider_1_out_3));  // open: Shang
  _4divider u_4divider_2 (.bcs({n4divider_1_out_3, A[3]}), .cs(B), .out_3(n4divider_2_out_3));  // open: Shang
  _4divider u_4divider_3 (.bcs({n4divider_2_out_3, A[2]}), .cs(B), .out_3(n4divider_3_out_3));  // open: Shang
  _4divider u_4divider_4 (.bcs({n4divider_3_out_3, A[1]}), .cs(B), .out_3(n4divider_4_out_3));  // open: Shang
  _4divider u_4divider_5 (.bcs({n4divider_4_out_3, A[0]}), .cs(B), .out_3(n4divider_5_out_3));  // open: Shang
  _4divider u_4divider_6 (.bcs({n4divider_5_out_3, 1'b0}), .cs(B), .out_3(n4divider_6_out_3));  // open: Shang
  _4divider u_4divider_7 (.bcs({n4divider_6_out_3, 1'b0}), .cs(B), .out_3(n4divider_7_out_3));  // open: Shang
  _4divider u_4divider_8 (.bcs({n4divider_7_out_3, 1'b0}), .cs(B), .out_3(C[2:0]));  // open: Shang

  assign C[10:3] = A;

  // Other names for the same wires on the sheet: cs[3:0] = B
endmodule
