// Logisim project fsm.circ as structural Verilog
module fsm (
  input  clr,
  input  [1:0] in,
  output out_3
);

  wire clock_1_out, next_state_1_ss0, next_state_1_ss1, register_1_q, register_2_q, reset_1_x, reset_2_x;

  next_state next_state_1 (
    .s1(register_1_q), .s0(register_2_q), .in1(in[1]), .in0(in[0]), .ss1(next_state_1_ss1),
    .ss0(next_state_1_ss0));
  reset reset_1 (.a(clr), .b(next_state_1_ss1), .x(reset_1_x));
  reset reset_2 (.a(clr), .b(next_state_1_ss0), .x(reset_2_x));
  Register #(.width(1)) register_1 (.D(reset_1_x), .Q(register_1_q), .clk(clock_1_out));  // open: en, clr
  Register #(.width(1)) register_2 (.D(reset_2_x), .Q(register_2_q), .clk(clock_1_out));  // open: en, clr
  Clock clock_1 (.out(clock_1_out));
  \output  output_1 (.s1(register_1_q), .s0(register_2_q), .in1(in[1]), .in0(in[0]), .out(out_3));
endmodule

module next_state (
  input  s1,
  input  s0,
  input  in1,
  input  in0,
  output ss1,
  output ss0
);

  wire and_1_out, and_2_out, and_3_out, and_4_out, not_1_out, not_2_out, not_3_out, not_4_out, not_5_out;

  and and_1 (and_1_out, s0, not_1_out);
  not not_1 (not_1_out, in0);
  and and_2 (and_2_out, s1, s0, in1);
  not not_2 (not_2_out, s1);
  not not_3 (not_3_out, in1);
  and and_3 (and_3_out, not_2_out, not_3_out, in0);
  not not_4 (not_4_out, s0);
  and and_4 (and_4_out, not_4_out, not_5_out, in0);
  not not_5 (not_5_out, in1);
  or or_1 (ss1, and_1_out, and_2_out);
  or or_2 (ss0, and_3_out, and_4_out);
endmodule

module \output  (
  input  s1,
  input  s0,
  input  in1,
  input  in0,
  output out
);

  wire not_1_out, not_2_out;

  and and_1 (out, s1, not_1_out, not_2_out);
  not not_1 (not_1_out, s0);
  not not_2 (not_2_out, in0);
endmodule

module reset (
  input  a,
  input  b,
  output x
);

  wire not_1_out;

  not not_1 (not_1_out, a);
  and and_1 (x, not_1_out, b);
endmodule
