// Logisim project grf.circ as structural Verilog
module grf (
  input  clk,
  input  Reset,
  input  WE,
  input  [4:0] A1,
  input  [4:0] A2,
  input  [4:0] A3,
  input  [31:0] WD,
  output [31:0] RD1,
  output [31:0] RD2
);

  wire _100, _101, _102, _103, _104, _105, _106, _107, _108, _109, _110, _111, _112, _113, _114, _115, _116,
       _117, _118, _119, _120, _121, _122, _123, _124, _125, _126, _127, _128, _129, _130, _131;
  wire [31:0] _00, _01, _02, _03, _04, _05, _06, _07, _08, _09, _10, _11, _12, _13, _14, _15, _16, _17, _18,
       _19, _20, _21, _22, _23, _24, _25, _26, _27, _28, _29, _30, _31;

  Register #(.width(32)) u__01 (.Q(_00));  // open: D, en, clk, clr
  Register #(.width(32)) _01_2 (.D(WD), .en(_101), .Q(_01), .clk(clk), .clr(Reset));
  Register #(.width(32)) u__02 (.D(WD), .en(_102), .Q(_02), .clk(clk), .clr(Reset));
  Register #(.width(32)) u__03 (.D(WD), .en(_103), .Q(_03), .clk(clk), .clr(Reset));
  Multiplexer #(.select(5), .width(32)) multiplexer_1 (
    .in0(_00), .in1(_01), .in2(_02), .in3(_03), .in4(_04), .in5(_05), .in6(_06), .in7(_07), .in8(_08),
    .in9(_09), .in10(_10), .in11(_11), .in12(_12), .in13(_13), .in14(_14), .in15(_15), .in16(_16),
    .in17(_17), .in18(_18), .in19(_19), .in20(_20), .in21(_21), .in22(_22), .in23(_23), .in24(_24),
    .in25(_25), .in26(_26), .in27(_27), .in28(_28), .in29(_29), .in30(_30), .in31(_31), .out(RD1), .sel(A1));  // open: en
  Register #(.width(32)) u__04 (.D(WD), .en(_104), .Q(_04), .clk(clk), .clr(Reset));
  Register #(.width(32)) u__05 (.D(WD), .en(_105), .Q(_05), .clk(clk), .clr(Reset));
  Register #(.width(32)) u__06 (.D(WD), .en(_106), .Q(_06), .clk(clk), .clr(Reset));
  Register #(.width(32)) u__07 (.D(WD), .en(_107), .Q(_07), .clk(clk), .clr(Reset));
  Register #(.width(32)) u__08 (.D(WD), .en(_108), .Q(_08), .clk(clk), .clr(Reset));
  Register #(.width(32)) u__09 (.D(WD), .en(_109), .Q(_09), .clk(clk), .clr(Reset));
  Register #(.width(32)) u__10 (.D(WD), .en(_110), .Q(_10), .clk(clk), .clr(Reset));
  Register #(.width(32)) u__11 (.D(WD), .en(_111), .Q(_11), .clk(clk), .clr(Reset));
  Multiplexer #(.select(5), .width(32)) multiplexer_2 (
    .in0(_00), .in1(_01), .in2(_02), .in3(_03), .in4(_04), .in5(_05), .in6(_06), .in7(_07), .in8(_08),
    .in9(_09), .in10(_10), .in11(_11), .in12(_12), .in13(_13), .in14(_14), .in15(_15), .in16(_16),
    .in17(_17), .in18(_18), .in19(_19), .in20(_20), .in21(_21), .in22(_22), .in23(_23), .in24(_24),
    .in25(_25), .in26(_26), .in27(_27), .in28(_28), .in29(_29), .in30(_30), .in31(_31), .out(RD2), .sel(A2));  // open: en
  Register #(.width(32)) u__12 (.D(WD), .en(_112), .Q(_12), .clk(clk), .clr(Reset));
  Register #(.width(32)) u__13 (.D(WD), .en(_113), .Q(_13), .clk(clk), .clr(Reset));
  Register #(.width(32)) u__14 (.D(WD), .en(_114), .Q(_14), .clk(clk), .clr(Reset));
  Register #(.width(32)) u__15 (.D(WD), .en(_115), .Q(_15), .clk(clk), .clr(Reset));
  Register #(.width(32)) u__16 (.D(WD), .en(_116), .Q(_16), .clk(clk), .clr(Reset));
  Register #(.width(32)) u__17 (.D(WD), .en(_117), .Q(_17), .clk(clk), .clr(Reset));
  Register #(.width(32)) u__18 (.D(WD), .en(_118), .Q(_18), .clk(clk), .clr(Reset));
  Register #(.width(32)) u__19 (.D(WD), .en(_119), .Q(_19), .clk(clk), .clr(Reset));
  Demultiplexer #(.select(5)) demultiplexer_1 (
    .out0(_100), .out1(_101), .out2(_102), .out3(_103), .out4(_104), .out5(_105), .out6(_106), .out7(_107),
    .out8(_108), .out9(_109), .out10(_110), .out11(_111), .out12(_112), .out13(_113), .out14(_114),
    .out15(_115), .out16(_116), .out17(_117), .out18(_118), .out19(_119), .out20(_120), .out21(_121),
    .out22(_122), .out23(_123), .out24(_124), .out25(_125), .out26(_126), .out27(_127), .out28(_128),
    .out29(_129), .out30(_130), .out31(_131), .in(WE), .sel(A3));  // open: en
  Register #(.width(32)) u__20 (.D(WD), .en(_120), .Q(_20), .clk(clk), .clr(Reset));
  Register #(.width(32)) u__21 (.D(WD), .en(_121), .Q(_21), .clk(clk), .clr(Reset));
  Register #(.width(32)) u__22 (.D(WD), .en(_122), .Q(_22), .clk(clk), .clr(Reset));
  Register #(.width(32)) u__23 (.D(WD), .en(_123), .Q(_23), .clk(clk), .clr(Reset));
  Register #(.width(32)) u__24 (.D(WD), .en(_124), .Q(_24), .clk(clk), .clr(Reset));
  Register #(.width(32)) u__25 (.D(WD), .en(_125), .Q(_25), .clk(clk), .clr(Reset));
  Register #(.width(32)) u__26 (.D(WD), .en(_126), .Q(_26), .clk(clk), .clr(Reset));
  Register #(.width(32)) u__27 (.D(WD), .en(_127), .Q(_27), .clk(clk), .clr(Reset));
  Register #(.width(32)) u__28 (.D(WD), .en(_128), .Q(_28), .clk(clk), .clr(Reset));
  Register #(.width(32)) u__29 (.D(WD), .en(_129), .Q(_29), .clk(clk), .clr(Reset));
  Register #(.width(32)) u__30 (.D(WD), .en(_130), .Q(_30), .clk(clk), .clr(Reset));
  Register #(.width(32)) u__31 (.D(WD), .en(_131), .Q(_31), .clk(clk), .clr(Reset));
endmodule
