// Logisim project CPU.circ as structural Verilog: 10 circuits, main circuit main
// Control
module main (
  input  RESET,
  output [31:0] out_2,
  output out_3,
  output [4:0] out_4,
  output [31:0] out_5,
  output out_6,
  output [4:0] out_7,
  output [31:0] out_8
);

  wire ALUSrc, and_1_out, Branch, CLK, Memread, MemtoReg, PCJump, RegDst, ZERO;
  wire [1:0] exp;
  wire [2:0] ALUOp;
  wire [4:0] rd, rs, rt;
  wire [5:0] func, opcode;
  wire [15:0] imm;
  wire [25:0] j_addr;
  wire [27:0] bit_extender_4_out, j_addr_exp;
  wire [31:0] alu_1_out_5, bit_extender_1_out, bit_extender_2_out, bit_extender_3_out, data_m_1_r,
       grf_1_out_8, imm_exp, imm_exp_beq, multiplexer_3_out, shifter_1_out;

  Clock clock_1 (.out(CLK));
  // Probe on out_2
  IFU ifu_1 (
    .imm(imm_exp_beq), .j_addr(j_addr_exp), .CLK(CLK), .Branch(and_1_out), .J(PCJump), .RE(RESET),
    .out_7(out_2));
  and and_1 (and_1_out, Branch, ZERO);
  assign bit_extender_1_out = {{16{1'b0}}, imm};  // Bit_Extender bit_extender_1
  assign bit_extender_2_out = {{16{imm[15]}}, imm};  // Bit_Extender bit_extender_2
  assign bit_extender_3_out = {{16{1'b0}}, imm};  // Bit_Extender bit_extender_3
  IFU_splitter ifu_splitter_1 (
    .in_1(out_2), .j_addr(j_addr), .imm(imm), .func(func), .rd(rd), .rt(rt), .rs(rs), .opcode(opcode));  // open: shamt
  Shifter #(.width(32)) shifter_1 (.in(bit_extender_3_out), .\dist (5'b10000), .out(shifter_1_out));
  // Probe on j_addr
  Multiplexer #(.select(2), .width(32)) multiplexer_1 (
    .in0(bit_extender_1_out), .in1(bit_extender_2_out), .in2(shifter_1_out), .out(imm_exp), .sel(exp));  // open: in3, en
  // Probe on opcode
  Multiplexer #(.width(5)) multiplexer_2 (.in0(rt), .in1(rd), .out(out_4), .sel(RegDst));  // open: en
  GRF grf_1 (
    .in_3(rs), .in_4(rt), .in_5(out_4), .in_6(out_5), .out_8(grf_1_out_8), .out_9(out_8), .in_7(CLK),
    .in_1(RESET), .in_2(out_3));
  assign bit_extender_4_out = {{2{1'b0}}, j_addr};  // Bit_Extender bit_extender_4
  control control_1 (
    .func(func), .opcode(opcode), .out_3(RegDst), .out_4(out_3), .out_5(ALUSrc), .out_6(Branch),
    .out_7(Memread), .out_8(out_6), .out_9(MemtoReg), .ALUCTRL(ALUOp), .out_11(exp), .PCjump(PCJump));
  Shifter #(.width(28)) shifter_2 (.in(bit_extender_4_out), .\dist (5'b00010), .out(j_addr_exp));
  Multiplexer #(.width(32)) multiplexer_3 (
    .in0(out_8), .in1(imm_exp), .out(multiplexer_3_out), .sel(ALUSrc));  // open: en
  Shifter #(.width(32)) shifter_3 (.in(imm_exp), .\dist (5'b00010), .out(imm_exp_beq));
  ALU alu_1 (.in_1(grf_1_out_8), .in_2(multiplexer_3_out), .ALUOp(ALUOp), .zero(ZERO), .out_5(alu_1_out_5));
  Data_M data_m_1 (
    .Address(alu_1_out_5), .WD(out_8), .WE(out_6), .CLK(CLK), .load(Memread), .RE(RESET), .OUTPUT(out_7),
    .R(data_m_1_r));
  Multiplexer #(.width(32)) multiplexer_4 (
    .in0(alu_1_out_5), .in1(data_m_1_r), .out(out_5), .sel(MemtoReg));  // open: en

  // Other names for the same wires on the sheet: Instr[31:0] = out_2; Memaddr[4:0] = out_7; MemData[31:0] = out_8;
  //   MemWrite = out_6; RegAddr[4:0] = out_4; RegWrite = out_3; WD[31:0] = out_5
endmodule

module Instruction_M (
  input  [4:0] in_1,
  output [31:0] out_2
);

  ROM #(.addrWidth(5), .dataWidth(32)) rom_1 (.addr(in_1), .data(out_2));  // open: sel
  // Probe on out_2

  // Notes on the sheet:
  //   contents of rom_1 (hex, n*v repeats v):
  //   34041000 34851234 808021 a48823 1085fffd 10900003 3c155555 2402000a c ac040000 ac050004 ac100008
  //   8c120004 3c0f2345 3c183456 8000c06
endmodule

module GRF (
  input  in_1,
  input  in_2,
  input  [4:0] in_3,
  input  [4:0] in_4,
  input  [4:0] in_5,
  input  [31:0] in_6,
  input  in_7,
  output [31:0] out_8,
  output [31:0] out_9
);

  wire _1, _2, _3, _4, _5, _6, _7, _8, _9, _10, _11, _12, _13, _14, _15, _16, _17, _18, _19, _20, _21, _22,
       _23, _24, _25, _26, _27, _28, _29, _30, _31;
  wire [31:0] _0a, _1a, _2a, _3a, _4a, _5a, _6a, _7a, _8a, _9a, _10a, _11a, _12a, _13a, _14a, _15a, _16a,
       _17a, _18a, _19a, _20a, _21a, _22a, _23a, _24a, _25a, _26a, _27a, _28a, _29a, _30a, _31a;

  Demultiplexer #(.select(5)) demultiplexer_1 (
    .out1(_1), .out2(_2), .out3(_3), .out4(_4), .out5(_5), .out6(_6), .out7(_7), .out8(_8), .out9(_9),
    .out10(_10), .out11(_11), .out12(_12), .out13(_13), .out14(_14), .out15(_15), .out16(_16), .out17(_17),
    .out18(_18), .out19(_19), .out20(_20), .out21(_21), .out22(_22), .out23(_23), .out24(_24), .out25(_25),
    .out26(_26), .out27(_27), .out28(_28), .out29(_29), .out30(_30), .out31(_31), .in(in_2), .sel(in_5));  // open: out0, en
  Register #(.width(32)) _0 (.D({32{1'b0}}), .en(in_2), .Q(_0a), .clk(in_7), .clr(in_1));
  Register #(.width(32)) _0_2 (.D(in_6), .en(_8), .Q(_8a), .clk(in_7), .clr(in_1));
  Register #(.width(32)) _0_3 (.D(in_6), .en(_16), .Q(_16a), .clk(in_7), .clr(in_1));
  Register #(.width(32)) _0_4 (.D(in_6), .en(_24), .Q(_24a), .clk(in_7), .clr(in_1));
  Register #(.width(32)) u__1 (.D(in_6), .en(_1), .Q(_1a), .clk(in_7), .clr(in_1));
  Register #(.width(32)) _0_5 (.D(in_6), .en(_9), .Q(_9a), .clk(in_7), .clr(in_1));
  Register #(.width(32)) _0_6 (.D(in_6), .en(_17), .Q(_17a), .clk(in_7), .clr(in_1));
  Register #(.width(32)) _0_7 (.D(in_6), .en(_25), .Q(_25a), .clk(in_7), .clr(in_1));
  Register #(.width(32)) _0_8 (.D(in_6), .en(_2), .Q(_2a), .clk(in_7), .clr(in_1));
  Register #(.width(32)) _0_9 (.D(in_6), .en(_10), .Q(_10a), .clk(in_7), .clr(in_1));
  Register #(.width(32)) _0_10 (.D(in_6), .en(_18), .Q(_18a), .clk(in_7), .clr(in_1));
  Register #(.width(32)) _0_11 (.D(in_6), .en(_26), .Q(_26a), .clk(in_7), .clr(in_1));
  Register #(.width(32)) _0_12 (.D(in_6), .en(_3), .Q(_3a), .clk(in_7), .clr(in_1));
  Register #(.width(32)) _0_13 (.D(in_6), .en(_11), .Q(_11a), .clk(in_7), .clr(in_1));
  Register #(.width(32)) _0_14 (.D(in_6), .en(_19), .Q(_19a), .clk(in_7), .clr(in_1));
  Register #(.width(32)) _0_15 (.D(in_6), .en(_27), .Q(_27a), .clk(in_7), .clr(in_1));
  Multiplexer #(.select(5), .width(32)) multiplexer_1 (
    .in0({32{1'b0}}), .in1(_1a), .in2(_2a), .in3(_3a), .in4(_4a), .in5(_5a), .in6(_6a), .in7(_7a), .in8(_8a),
    .in9(_9a), .in10(_10a), .in11(_11a), .in12(_12a), .in13(_13a), .in14(_14a), .in15(_15a), .in16(_16a),
    .in17(_17a), .in18(_18a), .in19(_19a), .in20(_20a), .in21(_21a), .in22(_22a), .in23(_23a), .in24(_24a),
    .in25(_25a), .in26(_26a), .in27(_27a), .in28(_28a), .in29(_29a), .in30(_30a), .in31(_31a), .out(out_9),
    .sel(in_4));  // open: en
  Register #(.width(32)) _0_16 (.D(in_6), .en(_4), .Q(_4a), .clk(in_7), .clr(in_1));
  Register #(.width(32)) _0_17 (.D(in_6), .en(_12), .Q(_12a), .clk(in_7), .clr(in_1));
  Register #(.width(32)) _0_18 (.D(in_6), .en(_20), .Q(_20a), .clk(in_7), .clr(in_1));
  Register #(.width(32)) _0_19 (.D(in_6), .en(_28), .Q(_28a), .clk(in_7), .clr(in_1));
  Register #(.width(32)) _0_20 (.D(in_6), .en(_5), .Q(_5a), .clk(in_7), .clr(in_1));
  Register #(.width(32)) _0_21 (.D(in_6), .en(_13), .Q(_13a), .clk(in_7), .clr(in_1));
  Register #(.width(32)) _0_22 (.D(in_6), .en(_21), .Q(_21a), .clk(in_7), .clr(in_1));
  Register #(.width(32)) _0_23 (.D(in_6), .en(_29), .Q(_29a), .clk(in_7), .clr(in_1));
  Register #(.width(32)) _0_24 (.D(in_6), .en(_6), .Q(_6a), .clk(in_7), .clr(in_1));
  Register #(.width(32)) _0_25 (.D(in_6), .en(_14), .Q(_14a), .clk(in_7), .clr(in_1));
  Register #(.width(32)) _0_26 (.D(in_6), .en(_22), .Q(_22a), .clk(in_7), .clr(in_1));
  Register #(.width(32)) _0_27 (.D(in_6), .en(_30), .Q(_30a), .clk(in_7), .clr(in_1));
  Multiplexer #(.select(5), .width(32)) multiplexer_2 (
    .in0({32{1'b0}}), .in1(_1a), .in2(_2a), .in3(_3a), .in4(_4a), .in5(_5a), .in6(_6a), .in7(_7a), .in8(_8a),
    .in9(_9a), .in10(_10a), .in11(_11a), .in12(_12a), .in13(_13a), .in14(_14a), .in15(_15a), .in16(_16a),
    .in17(_17a), .in18(_18a), .in19(_19a), .in20(_20a), .in21(_21a), .in22(_22a), .in23(_23a), .in24(_24a),
    .in25(_25a), .in26(_26a), .in27(_27a), .in28(_28a), .in29(_29a), .in30(_30a), .in31(_31a), .out(out_8),
    .sel(in_3));  // open: en
  Register #(.width(32)) _0_28 (.D(in_6), .en(_7), .Q(_7a), .clk(in_7), .clr(in_1));
  Register #(.width(32)) _0_29 (.D(in_6), .en(_15), .Q(_15a), .clk(in_7), .clr(in_1));
  Register #(.width(32)) _0_30 (.D(in_6), .en(_23), .Q(_23a), .clk(in_7), .clr(in_1));
  Register #(.width(32)) _0_31 (.D(in_6), .en(_31), .Q(_31a), .clk(in_7), .clr(in_1));

  // Other names for the same wires on the sheet: A1[4:0] = in_3; A2[4:0] = in_4; A3[4:0] = in_5; CLK = in_7;
  //   RD1[31:0] = out_8; RD2[31:0] = out_9; RESET = in_1; WD[31:0] = in_6; WE = in_2
endmodule

// DM
module Data_M (
  input  RE,
  input  CLK,
  input  WE,
  input  load,
  input  [31:0] Address,
  input  [31:0] WD,
  output [4:0] OUTPUT,
  output [31:0] R
);

  RAM #(.addrWidth(5), .dataWidth(32), .bus("separate")) ram_1 (
    .addr(Address[6:2]), .din(WD), .data(R), .str(WE), .clk(CLK), .ld(load), .clr(RE));  // open: sel

  assign OUTPUT = Address[6:2];
endmodule

module ALU (
  input  [31:0] in_1,
  input  [31:0] in_2,
  input  [2:0] ALUOp,
  output zero,
  output [31:0] out_5
);

  wire tunnel_t_t, tunnel_t_t_t, tunnel_t_t_t_t;
  wire [31:0] \or , tunnel, tunnel_t;

  Adder #(.width(32)) adder_1 (.a(in_1), .b(in_2), .out(tunnel));  // open: cin, cout
  Subtractor #(.width(32)) subtractor_1 (.a(in_1), .b(in_2), .out(tunnel_t));  // open: bin, bout
  Comparator #(.width(32), .mode("unsigned")) comparator_1 (
    .a(in_1), .b(in_2), .gt(tunnel_t_t_t_t), .eq(tunnel_t_t_t), .lt(tunnel_t_t));
  Comparator #(.width(32), .mode("unsigned")) comparator_2 (.a(tunnel_t), .b({32{1'b0}}), .eq(zero));  // open: gt, lt
  assign \or  = in_1 | in_2;  // OR_Gate or_1, 32 bits wide
  Multiplexer #(.select(3), .width(32)) multiplexer_1 (
    .in0(tunnel), .in1(tunnel_t), .in2(\or ), .out(out_5), .sel(ALUOp));  // open: in3, in4, in5, in6, in7, en

  // Other names for the same wires on the sheet: in1[31:0] = in_1; in2[31:0] = in_2
endmodule

// Control
module control (
  input  [5:0] func,
  input  [5:0] opcode,
  output out_3,
  output out_4,
  output out_5,
  output out_6,
  output out_7,
  output out_8,
  output out_9,
  output [2:0] ALUCTRL,
  output [1:0] out_11,
  output PCjump
);

  wire ctrl_and_1_addu, ctrl_and_1_beq, ctrl_and_1_j, ctrl_and_1_lui, ctrl_and_1_lw, ctrl_and_1_nop,
       ctrl_and_1_ori, ctrl_and_1_subu, ctrl_and_1_sw;

  ctrl_and ctrl_and_1 (
    .op5(opcode[5]), .op4(opcode[4]), .op3(opcode[3]), .op2(opcode[2]), .op1(opcode[1]), .op0(opcode[0]),
    .f5(func[5]), .f4(func[4]), .f3(func[3]), .f2(func[2]), .f1(func[1]), .f0(func[0]),
    .addu(ctrl_and_1_addu), .subu(ctrl_and_1_subu), .ori(ctrl_and_1_ori), .lw(ctrl_and_1_lw),
    .sw(ctrl_and_1_sw), .beq(ctrl_and_1_beq), .lui(ctrl_and_1_lui), .nop(ctrl_and_1_nop), .j(ctrl_and_1_j));
  ctrl_or ctrl_or_1 (
    .addu(ctrl_and_1_addu), .subu(ctrl_and_1_subu), .ori(ctrl_and_1_ori), .lw(ctrl_and_1_lw),
    .sw(ctrl_and_1_sw), .beq(ctrl_and_1_beq), .lui(ctrl_and_1_lui), .nop(ctrl_and_1_nop), .j(ctrl_and_1_j),
    .RegDst(out_3), .RegWrite(out_4), .ALUSrc(out_5), .PCSrc(out_6), .Memread(out_7), .Memwrite(out_8),
    .MemtoReg(out_9), .ALU0(ALUCTRL[0]), .ALU1(ALUCTRL[1]), .ALU2(ALUCTRL[2]), .exp0(out_11[0]),
    .exp1(out_11[1]), .PCJump(PCjump));
endmodule

module IFU (
  input  Branch,
  input  J,
  input  [31:0] imm,
  input  [27:0] j_addr,
  input  CLK,
  input  RE,
  output [31:0] out_7
);

  wire [31:0] adder_1_out, adder_2_out, multiplexer_1_out, multiplexer_2_out, register_1_q;

  Adder #(.width(32)) adder_1 (.a(register_1_q), .b(32'h4), .out(adder_1_out));  // open: cin, cout
  Adder #(.width(32)) adder_2 (.a(adder_1_out), .b(imm), .out(adder_2_out));  // open: cin, cout
  Multiplexer #(.width(32)) multiplexer_1 (
    .in0(adder_1_out), .in1(adder_2_out), .out(multiplexer_1_out), .sel(Branch));  // open: en
  Subtractor #(.width(32)) subtractor_1 (.b(32'h3000));  // open: a, out, bin, bout
  // Probe on {register_1_q[31:28], j_addr}
  Multiplexer #(.width(32)) multiplexer_2 (
    .in0(multiplexer_1_out), .in1({register_1_q[31:28], j_addr}), .out(multiplexer_2_out), .sel(J));  // open: en
  Register #(.width(32)) register_1 (.D(multiplexer_2_out), .Q(register_1_q), .clk(CLK), .clr(RE));  // open: en
  Instruction_M instruction_m_1 (.in_1(register_1_q[6:2]), .out_2(out_7));
endmodule

// IS
module IFU_splitter (
  input  [31:0] in_1,
  output [25:0] j_addr,
  output [15:0] imm,
  output [5:0] func,
  output [4:0] shamt,
  output [4:0] rd,
  output [4:0] rt,
  output [4:0] rs,
  output [5:0] opcode
);


  assign func = in_1[5:0];
  assign imm = in_1[15:0];
  assign j_addr = in_1[25:0];
  assign opcode = in_1[31:26];
  assign rd = in_1[15:11];
  assign rs = in_1[25:21];
  assign rt = in_1[20:16];
  assign shamt = in_1[10:6];
endmodule

module ctrl_and (
  input  op5,
  input  op4,
  input  op3,
  input  op2,
  input  op1,
  input  op0,
  input  f5,
  input  f4,
  input  f3,
  input  f2,
  input  f1,
  input  f0,
  output addu,
  output subu,
  output ori,
  output lw,
  output sw,
  output beq,
  output lui,
  output nop,
  output j
);

  wire not_1_out, not_2_out, not_3_out, not_4_out, not_5_out, not_6_out, not_7_out, not_8_out, not_9_out,
       not_10_out, not_11_out, not_12_out;

  not not_1 (not_1_out, op5);
  not not_2 (not_2_out, op4);
  not not_3 (not_3_out, op2);
  not not_4 (not_4_out, op3);
  not not_5 (not_5_out, op0);
  not not_6 (not_6_out, f5);
  not not_7 (not_7_out, op1);
  not not_8 (not_8_out, f4);
  not not_9 (not_9_out, f2);
  not not_10 (not_10_out, f3);
  not not_11 (not_11_out, f1);
  not not_12 (not_12_out, f0);
  and and_1 (addu, not_1_out, not_2_out, not_4_out, not_3_out, not_7_out, not_5_out, f5, f0, not_8_out, not_10_out, not_9_out, not_11_out);
  and and_2 (subu, not_1_out, not_2_out, not_4_out, not_3_out, not_7_out, not_5_out, f5, not_8_out, not_10_out, not_9_out, f1, f0);
  and and_3 (ori, not_1_out, not_2_out, op3, op2, not_7_out, op0);
  and and_4 (lw, not_2_out, op5, not_4_out, not_3_out, op1, op0);
  and and_5 (sw, op5, not_2_out, op3, not_3_out, op1, op0);
  and and_6 (beq, not_2_out, not_1_out, not_4_out, op2, not_7_out, not_5_out);
  and and_7 (lui, not_1_out, not_2_out, op3, op2, op1, op0);
  and and_8 (nop, not_1_out, not_2_out, not_4_out, not_7_out, not_3_out, not_5_out);
  and and_9 (j, not_2_out, not_1_out, not_4_out, not_3_out, op1, not_5_out);
endmodule

module ctrl_or (
  input  addu,
  input  subu,
  input  ori,
  input  lw,
  input  sw,
  input  beq,
  input  lui,
  input  nop,
  input  j,
  output RegDst,
  output RegWrite,
  output ALUSrc,
  output PCSrc,
  output Memread,
  output Memwrite,
  output MemtoReg,
  output ALU0,
  output ALU1,
  output ALU2,
  output exp0,
  output exp1,
  output PCJump
);

  or or_1 (RegDst, addu, subu);
  or or_2 (RegWrite, lui, addu, subu, lw, ori);
  or or_3 (ALUSrc, ori, sw, lw, lui);
  buf or_4 (PCSrc, beq);  // OR_Gate
  // OR_Gate or_5 is placed but not wired
  buf or_6 (Memread, lw);  // OR_Gate
  buf or_7 (Memwrite, sw);  // OR_Gate
  buf or_8 (MemtoReg, lw);  // OR_Gate
  or or_9 (ALU0, subu, beq);
  or or_10 (ALU1, ori, beq);
  or or_11 (exp0, lw, sw, beq);
  buf or_12 (exp1, lui);  // OR_Gate
  buf or_13 (PCJump, j);  // OR_Gate

  assign ALU2 = 1'b0;
endmodule
